# Fritzing sketch Sketch Cargador Solar (saved by Fritzing 1.0.3b)
# 18650 Li-ion Battery: CC-BY Dr Kristofer Chan, King's College London/Remote-research.org
breadboards: 1

parts:
  Componente3 = Arduino Uno (Rev3)
  MG90S = Basic Servo
  R9 = Resistor [tolerance=±5% power=0.25W resistance=10k package=THT]
  R10 = Resistor [tolerance=±5% power=0.25W resistance=10k package=THT]
  R11 = Resistor [tolerance=±5% power=0.25W resistance=10k package=THT]
  R12 = Resistor [tolerance=±5% power=0.25W resistance=10k package=THT]
  LDR3 = Photocell (LDR) [power=0.25W dark_resistance_@0.01lx=300kΩ light_resistance_@100lx=400Ω luminance=10lx package=THT]
  LDR4 = Photocell (LDR) [power=0.25W dark_resistance_@0.01lx=300kΩ light_resistance_@100lx=400Ω luminance=10lx package=THT]
  LDR2 = Photocell (LDR) [power=0.25W dark_resistance_@0.01lx=300kΩ light_resistance_@100lx=400Ω luminance=10lx package=THT]
  LDR1 = Photocell (LDR) [power=0.25W dark_resistance_@0.01lx=300kΩ light_resistance_@100lx=400Ω luminance=10lx package=THT]
  HW-106 = 0.9v-5V booster usb output
  HW-106_2 = 0.9v-5V booster usb output
  Panel_5V_55mA = Solar Cell Mod
  MG90S_2 = Basic Servo
  TP4056 = TP4056 [chip_label=TP4056 package="DIP (Dual Inline) [THT]"]
  BAT-LIPO = 18650 Li-ion Battery [package=battery-18650]

nets:
  N1: Componente3.A0, R10.Pin_0, LDR2.pin_1
  N2: Componente3.A1, R11.Pin_1, LDR4.pin_1
  N3: Componente3.A2, R9.Pin_1, R10.Pin_1, R11.Pin_0, R12.Pin_0
  N4: Componente3.A3, R9.Pin_0, LDR1.pin_0
  N5: Componente3.D9_PWM, MG90S.pulse
  N6: Componente3.D10_PWM/SS, MG90S_2.pulse
  VCC: Componente3.5V, MG90S.vcc, LDR3.pin_1, LDR4.pin_0, LDR2.pin_0, LDR1.pin_1, MG90S_2.vcc
  GND: Componente3.GND, MG90S.gnd, R12.Pin_1, LDR3.pin_0, MG90S_2.gnd
  N7: HW-106.pin1, HW-106.pin4, HW-106_2.pin1, HW-106_2.pin4, TP4056.pin6
  N8: HW-106.pin2, HW-106_2.pin2, TP4056.pin3
  N9: Panel_5V_55mA.+, TP4056.pin1
  N10: Panel_5V_55mA.-, TP4056.pin2
  N11: TP4056.pin4, BAT-LIPO.+
  N12: TP4056.pin5, BAT-LIPO.-

custom parts:
  0.9v-5V booster usb output: 0.9 V ~ 5 V up 5 V DC - DC booster module.
  TP4056: A DIP stand-in part for whatever IC you want. With 6 pins on a 300mil dual inline package (DIP) footprint.
  18650 Li-ion Battery: 18650 li-ion Battery Standard 18650 battery with interactive connectors Creative Common Attribution 4.0 International (CC-BY 4.0) license. Any use of this part requires attribution of Dr Kristofer Chan, Department of Geography, King's College London. Contact kristofer.chan [at] kcl.ac.uk OR kris [at] remote-research.org for further information.
